# Fritzing sketch Armax (saved by Fritzing 0.9.4)
breadboards: 1

parts:
  Part1 = InvenSense MPU6050
  OLED_I2C1 = OLED 128x64 I2C Monochrome Display
  Part2 = Bluetooth HC-05 Macho
  Parts1 = SparkFun RedBoard [part_number=DEV-12757]
  SP1 = SPEAKER [package=pcb_mount_speaker]

nets:
  VCC: Part1.VCC, OLED_I2C1.VDD, Part2.VCC, Parts1.5V, SP1.-
  GND: Part1.GND, OLED_I2C1.GND, Part2.GND, Parts1.GND
  N1: Part1.SCL, OLED_I2C1.SCK, Parts1.A5/SCL
  N2: Part1.SDA, OLED_I2C1.SDA, Parts1.A4/SDA
  N3: Part2.TXD, Parts1.D11_PWM/MOSI
  N4: Part2.RXD, Parts1.D10_PWM/SS
  N5: Parts1.D8, SP1.+

custom parts:
  SparkFun RedBoard: At SparkFun we use many Arduinos and we’re always looking for the simplest, most stable one. Each board is a bit different and no one board has everything we want, so we decided to make our own version that combines all our favorite features. The RedBoard combines the simplicity of the UNO’s Optiboot bootloader (which is used in the Pro series), the stability of the FTDI (which we all missed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
